// Logisim project mini_project (2).circ as structural Verilog: 8 circuits, main circuit main
module main (
  input  L,
  input  t1,
  input  t2,
  input  t3,
  input  m01,
  input  m02,
  input  m11,
  input  m12,
  input  clk,
  output t1_2,
  output t2_2,
  output t3_2,
  output m01_2,
  output m02_2,
  output m11_2,
  output m12_2
);

  wire and_1_out, and_2_out, and_3_out, and_4_out, and_5_out, and_6_out, and_7_out, and_8_out, and_9_out,
       and_10_out, and_11_out, and_12_out, and_13_out, and_14_out, not_1_out, not_2_out, or_1_out, or_2_out,
       or_3_out, or_4_out, or_5_out, or_6_out, or_7_out;

  not not_1 (not_1_out, L);
  not not_2 (not_2_out, not_1_out);
  and and_1 (and_1_out, t1_2, not_1_out);
  and and_2 (and_2_out, t1, not_2_out);
  and and_3 (and_3_out, t2_2, not_1_out);
  and and_4 (and_4_out, t2, not_2_out);
  and and_5 (and_5_out, t3_2, not_1_out);
  and and_6 (and_6_out, t3, not_2_out);
  and and_7 (and_7_out, m01_2, not_1_out);
  and and_8 (and_8_out, m01, not_2_out);
  and and_9 (and_9_out, m02_2, not_1_out);
  and and_10 (and_10_out, m02, not_2_out);
  and and_11 (and_11_out, m11_2, not_1_out);
  and and_12 (and_12_out, m11, not_2_out);
  and and_13 (and_13_out, m12_2, not_1_out);
  and and_14 (and_14_out, m12, not_2_out);
  or or_1 (or_1_out, and_1_out, and_2_out);
  or or_2 (or_2_out, and_3_out, and_4_out);
  or or_3 (or_3_out, and_5_out, and_6_out);
  or or_4 (or_4_out, and_7_out, and_8_out);
  or or_5 (or_5_out, and_9_out, and_10_out);
  or or_6 (or_6_out, and_11_out, and_12_out);
  or or_7 (or_7_out, and_13_out, and_14_out);
  D_Flip_Flop d_ff_1 (.clk(clk), .D(or_1_out), .Q(t1_2));  // open: Qn, preset, en, reset
  D_Flip_Flop d_ff_2 (.clk(clk), .D(or_2_out), .Q(t2_2));  // open: Qn, preset, en, reset
  D_Flip_Flop d_ff_3 (.clk(clk), .D(or_3_out), .Q(t3_2));  // open: Qn, preset, en, reset
  D_Flip_Flop d_ff_4 (.clk(clk), .D(or_4_out), .Q(m01_2));  // open: Qn, preset, en, reset
  D_Flip_Flop d_ff_5 (.clk(clk), .D(or_5_out), .Q(m02_2));  // open: Qn, preset, en, reset
  D_Flip_Flop d_ff_6 (.clk(clk), .D(or_6_out), .Q(m11_2));  // open: Qn, preset, en, reset
  D_Flip_Flop d_ff_7 (.clk(clk), .D(or_7_out), .Q(m12_2));  // open: Qn, preset, en, reset
endmodule

module loadRegister (
  input  in_1,
  input  in_2,
  input  in_3,
  input  in_4,
  input  MORNING,
  input  in_6,
  input  in_7,
  input  MEDICINE,
  input  in_9,
  input  in_10,
  input  MEDICINE_2,
  input  in_12,
  input  in_13,
  input  in_14,
  input  in_15,
  input  in_16,
  input  medicine_1,
  input  in_18,
  input  medicine_2_2,
  input  in_20,
  input  in_21,
  input  in_22,
  input  in_23,
  input  NIGHT_TIME,
  input  in_25,
  input  in_26,
  input  medicine_1_2,
  input  medicine_2_3,
  input  in_29,
  input  Body_Pains,
  input  fever,
  input  Cold,
  output out_33,
  output TIME__COUNTER,
  output out_35,
  output out_36,
  output out_37,
  output Cetrizine,
  output out_39
);

  wire and_1_out, and_2_out, and_3_out, and_4_out, bcd_to_seven_segment_1_a, bcd_to_seven_segment_1_b,
       bcd_to_seven_segment_1_c, bcd_to_seven_segment_1_d, bcd_to_seven_segment_1_e,
       bcd_to_seven_segment_1_f, bcd_to_seven_segment_1_g, clock_1_out, comparator_1_out_7,
       comparator_2_out_7, comparator_3_out_7, decoder_1_d0, decoder_1_d1, decoder_1_d2, decoder_1_d3,
       decoder_2_d0, decoder_2_d1, decoder_2_d2, decoder_2_d3, decoder_3_d0, decoder_3_d1, decoder_3_d2,
       decoder_3_d3, decoder_4_d0, decoder_4_d1, decoder_4_d2, decoder_4_d3, decoder_5_d0, decoder_5_d1,
       decoder_5_d2, decoder_5_d3, decoder_6_d0, decoder_6_d1, decoder_6_d2, decoder_6_d3, main_1_m01_2,
       main_1_m02_2, main_1_m11_2, main_1_m12_2, main_1_t1_2, main_1_t2_2, main_1_t3_2, main_2_m01_2,
       main_2_m02_2, main_2_m11_2, main_2_m12_2, main_2_t1_2, main_2_t2_2, main_2_t3_2, main_3_m01_2,
       main_3_m02_2, main_3_m11_2, main_3_m12_2, main_3_t1_2, main_3_t2_2, main_3_t3_2, not_1_out,
       number_of_med_1_out_2, number_of_med_2_out_2, number_of_med_3_out_2, or_2_out, or_3_out, or_4_out,
       or_5_out;

  Clock clock_1 (.out(clock_1_out));
  T_Flip_Flop t_ff_1 (.clk(clock_1_out), .T(in_2), .Q(out_35));  // open: Qn, preset, reset, en
  T_Flip_Flop t_ff_2 (.clk(clock_1_out), .T(out_35), .Q(TIME__COUNTER));  // open: Qn, preset, reset, en
  and and_1 (and_1_out, out_35, TIME__COUNTER);
  main main_1 (
    .L(in_3), .t1(in_4), .t2(MORNING), .t3(in_6), .m01(in_7), .m02(MEDICINE), .m11(in_10), .m12(MEDICINE_2),
    .t1_2(main_1_t1_2), .t2_2(main_1_t2_2), .t3_2(main_1_t3_2), .m01_2(main_1_m01_2), .m02_2(main_1_m02_2),
    .m11_2(main_1_m11_2), .m12_2(main_1_m12_2), .clk(clock_1_out));
  main main_2 (
    .L(in_13), .t1(in_14), .t2(in_15), .t3(in_16), .m01(medicine_1), .m02(in_18), .m11(medicine_2_2),
    .m12(in_20), .t1_2(main_2_t1_2), .t2_2(main_2_t2_2), .t3_2(main_2_t3_2), .m01_2(main_2_m01_2),
    .m02_2(main_2_m02_2), .m11_2(main_2_m11_2), .m12_2(main_2_m12_2), .clk(clock_1_out));
  main main_3 (
    .L(in_22), .t1(in_23), .t2(NIGHT_TIME), .t3(in_25), .m01(in_26), .m02(medicine_1_2), .m11(medicine_2_3),
    .m12(in_29), .t1_2(main_3_t1_2), .t2_2(main_3_t2_2), .t3_2(main_3_t3_2), .m01_2(main_3_m01_2),
    .m02_2(main_3_m02_2), .m11_2(main_3_m11_2), .m12_2(main_3_m12_2), .clk(clock_1_out));
  and and_2 (and_2_out, Cold, fever);
  and and_3 (and_3_out, fever, Body_Pains);
  and and_4 (and_4_out, Cold, Body_Pains);
  T_Flip_Flop t_ff_3 (.clk(clock_1_out), .T(and_1_out), .Q(out_33));  // open: Qn, preset, reset, en
  comparator comparator_1 (
    .in_1(main_1_t1_2), .in_2(out_35), .in_3(main_1_t2_2), .in_4(TIME__COUNTER), .in_5(main_1_t3_2),
    .in_6(out_33), .out_7(comparator_1_out_7));
  comparator comparator_2 (
    .in_1(main_2_t1_2), .in_2(out_35), .in_3(main_2_t2_2), .in_4(TIME__COUNTER), .in_5(main_2_t3_2),
    .in_6(out_33), .out_7(comparator_2_out_7));
  comparator comparator_3 (
    .in_1(main_3_t1_2), .in_2(out_35), .in_3(main_3_t2_2), .in_4(TIME__COUNTER), .in_5(main_3_t3_2),
    .in_6(out_33), .out_7(comparator_3_out_7));
  or or_1 (out_39, and_2_out, and_3_out, and_4_out);
  not not_1 (not_1_out, out_39);
  decoder decoder_1 (
    .en(comparator_1_out_7), .x(main_1_m01_2), .y(main_1_m02_2), .d0(decoder_1_d0), .d1(decoder_1_d1),
    .d2(decoder_1_d2), .d3(decoder_1_d3));
  decoder decoder_2 (
    .en(comparator_1_out_7), .x(main_1_m11_2), .y(main_1_m12_2), .d0(decoder_2_d0), .d1(decoder_2_d1),
    .d2(decoder_2_d2), .d3(decoder_2_d3));
  decoder decoder_3 (
    .en(comparator_2_out_7), .x(main_2_m01_2), .y(main_2_m02_2), .d0(decoder_3_d0), .d1(decoder_3_d1),
    .d2(decoder_3_d2), .d3(decoder_3_d3));
  decoder decoder_4 (
    .en(comparator_2_out_7), .x(main_2_m11_2), .y(main_2_m12_2), .d0(decoder_4_d0), .d1(decoder_4_d1),
    .d2(decoder_4_d2), .d3(decoder_4_d3));
  decoder decoder_5 (
    .en(comparator_3_out_7), .x(main_3_m01_2), .y(main_3_m02_2), .d0(decoder_5_d0), .d1(decoder_5_d1),
    .d2(decoder_5_d2), .d3(decoder_5_d3));
  decoder decoder_6 (
    .en(comparator_3_out_7), .x(main_3_m11_2), .y(main_3_m12_2), .d0(decoder_6_d0), .d1(decoder_6_d1),
    .d2(decoder_6_d2), .d3(decoder_6_d3));
  bcd_to_seven_segment bcd_to_seven_segment_1 (
    .A3(in_1), .A2(out_33), .A1(TIME__COUNTER), .A0(out_35), .a(bcd_to_seven_segment_1_a),
    .b(bcd_to_seven_segment_1_b), .c(bcd_to_seven_segment_1_c), .d(bcd_to_seven_segment_1_d),
    .e(bcd_to_seven_segment_1_e), .f(bcd_to_seven_segment_1_f), .g(bcd_to_seven_segment_1_g));
  and and_5 (out_36, Body_Pains, not_1_out);
  and and_6 (out_37, fever, not_1_out);
  and and_7 (Cetrizine, Cold, not_1_out);
  _7_Segment_Display u_7_segment_display_1 (
    .g(bcd_to_seven_segment_1_g), .f(bcd_to_seven_segment_1_f), .a(bcd_to_seven_segment_1_a),
    .b(bcd_to_seven_segment_1_b), .e(bcd_to_seven_segment_1_e), .d(bcd_to_seven_segment_1_d),
    .c(bcd_to_seven_segment_1_c));  // open: dp
  or or_2 (or_2_out, decoder_2_d0, decoder_1_d0, decoder_6_d0, decoder_4_d0, decoder_3_d0, decoder_5_d0);
  or or_3 (or_3_out, decoder_6_d1, decoder_5_d1, decoder_1_d1, decoder_2_d1, decoder_4_d1, decoder_3_d1);
  or or_4 (or_4_out, decoder_4_d2, decoder_1_d2, decoder_2_d2, decoder_5_d2, decoder_3_d2, decoder_6_d2);
  or or_5 (or_5_out, decoder_2_d3, decoder_3_d3, decoder_1_d3, decoder_4_d3, decoder_5_d3, decoder_6_d3);
  LED led_1 (.in(or_2_out));
  LED led_2 (.in(or_3_out));
  LED led_3 (.in(or_4_out));
  LED led_4 (.in(or_5_out));
  number_of_med number_of_med_1 (.in_1(in_9), .out_2(number_of_med_1_out_2));
  LED led_5 (.in(number_of_med_1_out_2));
  LED led_6 (.in(number_of_med_2_out_2));
  number_of_med number_of_med_2 (.in_1(in_12), .out_2(number_of_med_2_out_2));
  number_of_med number_of_med_3 (.in_1(in_21), .out_2(number_of_med_3_out_2));
  LED led_7 (.in(number_of_med_3_out_2));

  // Notes on the sheet:
  //   SWITCH ON COUNTER
  //   SWITCH ON MORNING REGISTER
  //   TIME
  //   SWITCH FOR MIDDAY REGISTER
  //   MIDDAY TIME
  //   SWITCH FOR NIGHT
  //   Basic Medicine Requirement:
  //   Register_MORN
  //   REGISTER_MID
  //   REGISTER_NIGHT
  //   Comparator
  //   Comparator
  //   Comparator
  //   6
  //   Decoder
  //   Tylenol
  //   Acetaminophen
  //   Paracetamol
  //   When Clock pulse is trggered, it will activate the
  //   whole circuit and provides indication of medicine to be 
  //   taken at that time.
  //   MEDICINE 3
  //   NO MEDICINE
  //   MEDICINE !
  //   MEDICINE 2
  //   Issues Warning If Tablets are to be reloaded
endmodule

module comparator (
  input  in_1,
  input  in_2,
  input  in_3,
  input  in_4,
  input  in_5,
  input  in_6,
  output out_7
);

  wire xnor_1_out, xnor_2_out, xnor_3_out;

  xnor xnor_1 (xnor_1_out, in_1, in_2);
  xnor xnor_2 (xnor_2_out, in_3, in_4);
  xnor xnor_3 (xnor_3_out, in_5, in_6);
  and and_1 (out_7, xnor_1_out, xnor_2_out, xnor_3_out);
endmodule

module decoder (
  input  en,
  input  x,
  input  y,
  output d0,
  output d1,
  output d2,
  output d3
);

  wire and_1_out, and_2_out, and_3_out, and_4_out, not_1_out, not_2_out;

  not not_1 (not_1_out, x);
  not not_2 (not_2_out, y);
  and and_1 (and_1_out, not_1_out, not_2_out);
  and and_2 (and_2_out, not_1_out, y);
  and and_3 (and_3_out, x, not_2_out);
  and and_4 (and_4_out, x, y);
  and and_5 (d0, en, and_1_out);
  and and_6 (d1, en, and_2_out);
  and and_7 (d2, en, and_3_out);
  and and_8 (d3, en, and_4_out);
endmodule

module bcd_to_seven_segment (
  input  A3,
  input  A2,
  input  A1,
  input  A0,
  output a,
  output b,
  output c,
  output d,
  output e,
  output f,
  output g
);

  wire and_1_out, and_2_out, and_3_out, and_4_out, and_5_out, and_6_out, and_7_out, and_8_out, and_9_out,
       not_1_out, not_2_out, not_3_out, not_4_out;

  not not_1 (not_1_out, A3);
  not not_2 (not_2_out, A2);
  not not_3 (not_3_out, A1);
  not not_4 (not_4_out, A0);
  and and_1 (and_1_out, A2, A0);
  and and_2 (and_2_out, not_2_out, not_4_out);
  and and_3 (and_3_out, A1, A0);
  and and_4 (and_4_out, not_3_out, not_4_out);
  or or_1 (c, A2, not_3_out, A0);
  and and_5 (and_5_out, A1, not_4_out);
  and and_6 (and_6_out, not_2_out, A1);
  and and_7 (and_7_out, A2, not_3_out);
  and and_8 (and_8_out, A2, not_4_out);
  and and_9 (and_9_out, A0, and_7_out);
  or or_2 (a, and_1_out, and_2_out, A3, A1);
  or or_3 (d, A3, and_2_out, and_5_out, and_6_out, and_9_out);
  or or_4 (b, and_3_out, and_4_out, not_2_out);
  or or_5 (e, and_2_out, and_5_out);
  or or_6 (f, and_4_out, and_7_out, A3, and_8_out);
  or or_7 (g, and_5_out, and_6_out, A3, and_7_out);
endmodule

module number_of_med (
  input  in_1,
  output out_2
);

  wire and_1_out, and_2_out, d_ff_1_q, d_ff_2_q, d_ff_3_q, nor_1_out, not_1_out, or_1_out, or_2_out,
       xnor_1_out;

  and and_1 (and_1_out, d_ff_3_q, d_ff_1_q);
  and and_2 (and_2_out, d_ff_2_q, d_ff_1_q);
  nor nor_1 (nor_1_out, d_ff_2_q, d_ff_3_q, d_ff_1_q);
  not not_1 (not_1_out, d_ff_3_q);
  D_Flip_Flop d_ff_1 (.clk(in_1), .D(or_1_out), .Q(d_ff_1_q));  // open: Qn, preset, en, reset
  or or_1 (or_1_out, and_1_out, and_2_out, nor_1_out);
  xnor xnor_1 (xnor_1_out, d_ff_2_q, d_ff_3_q);
  D_Flip_Flop d_ff_2 (.clk(in_1), .D(xnor_1_out), .Q(d_ff_2_q));  // open: Qn, preset, en, reset
  D_Flip_Flop d_ff_3 (.clk(in_1), .D(not_1_out), .Q(d_ff_3_q));  // open: Qn, preset, en, reset
  or or_2 (or_2_out, d_ff_3_q, d_ff_2_q, d_ff_1_q);
  not not_2 (out_2, or_2_out);
endmodule

module _4_bitcounter (
  input  Toggle,
  input  Up_count,
  input  in_3,
  input  Reset,
  output out_5,
  output out_6,
  output out_7,
  output LSB
);

  wire and_1_out, and_2_out, and_3_out, and_4_out, and_5_out, and_6_out, j_k_ff_1_qn, j_k_ff_2_qn,
       j_k_ff_3_qn, not_1_out, not_2_out, or_1_out, or_2_out, or_3_out, or_4_out, sr_latch_1_q;

  sr_latch sr_latch_1 (.S(Up_count), .R(in_3), .Q(sr_latch_1_q));  // open: Q_prime
  or or_1 (or_1_out, in_3, Up_count);
  not not_1 (not_1_out, or_1_out);
  J_K_Flip_Flop j_k_ff_1 (
    .J(Toggle), .clk(not_1_out), .K(Toggle), .Q(LSB), .Qn(j_k_ff_1_qn), .reset(Reset));  // open: preset, en
  not not_2 (not_2_out, sr_latch_1_q);
  and and_1 (and_1_out, sr_latch_1_q, LSB);
  and and_2 (and_2_out, j_k_ff_1_qn, not_2_out);
  or or_2 (or_2_out, and_1_out, and_2_out);
  J_K_Flip_Flop j_k_ff_2 (
    .J(or_2_out), .clk(not_1_out), .K(or_2_out), .Q(out_7), .Qn(j_k_ff_2_qn), .reset(Reset));  // open: preset, en
  and and_3 (and_3_out, and_1_out, out_7);
  and and_4 (and_4_out, j_k_ff_2_qn, and_2_out);
  or or_3 (or_3_out, and_3_out, and_4_out);
  and and_5 (and_5_out, and_3_out, out_6);
  J_K_Flip_Flop j_k_ff_3 (
    .J(or_3_out), .clk(not_1_out), .K(or_3_out), .Q(out_6), .Qn(j_k_ff_3_qn), .reset(Reset));  // open: preset, en
  and and_6 (and_6_out, j_k_ff_3_qn, and_4_out);
  or or_4 (or_4_out, and_5_out, and_6_out);
  J_K_Flip_Flop j_k_ff_4 (
    .J(or_4_out), .clk(not_1_out), .K(or_4_out), .Q(out_5), .reset(Reset));  // open: Qn, preset, en

  // Notes on the sheet:
  //   SR Latch
  //   Clock
  //   10 bit synchronous up/down counter 
  //   MSB
  //   COUNT
endmodule

module sr_latch (
  input  S,
  input  R,
  output Q,
  output Q_prime
);

  nor nor_1 (Q, R, Q_prime);
  nor nor_2 (Q_prime, Q, S);
endmodule
